# Fritzing sketch shutterfingers (saved by Fritzing 0.8.3b)
stripboards: 1

parts:
  Digispark1 = Digispark
  LED1 = LED - 5mm [color="Red (633nm)" package="5 mm [THT]"]
  J1 = Basic Servo
  TRRS1 = Audio Jack (TRRS) 3.5mm [part_number="LUMBERG JEITA RC-5325A" package="RC-5325A [SMD]"]
  S1 = Pushbutton [package=THT]
  U2 = LIPO-110mAh [package=lipo-110]
  Part1 = USB LiPoly Charger
  R1 = Resistor [tolerance=±5% resistance=220 package=THT]

nets:
  VCC: Digispark1.VCC, J1.vcc, S1.leg1
  GND: Digispark1.GND, LED1.anode, J1.gnd, TRRS1.SLEEVE, TRRS1.RING2, U2.-, Part1.GND
  N1: Digispark1.P0, TRRS1.TIP
  N2: Digispark1.P1, R1.Pin_0
  N3: Digispark1.P2, TRRS1.RING1
  N4: Digispark1.P5, J1.pulse
  N5: LED1.cathode, R1.Pin_1
  N6: S1.leg0, U2.+, Part1.VBAT

notes:
  Power Cell - LiPo Charger/Booster PRT-11231
  2.5mm TRS jack

custom parts:
  Digispark: The Digispark is an Attiny85 based microcontroller development board similar to the Arduino line, only cheaper, smaller, and a bit less powerful. With a whole host of shields to extend its functionality and the ability to use the familiar Arduino IDE the Digispark is a great way to jump into electronics, or perfect for when an Arduino is too big or too much.
