# Fritzing sketch LiPoSpark (saved by Fritzing 0.8.3b)
breadboards: 1

parts:
  U1 = attiny85 [package=dip]
  X1 = USB Connectors [package=usb-minib]
  U2 = TPS61200 [package=qfn-10_pad]
  U3 = MCP73831 [package=sot23-5]
  JP1 = Header 2 [package=jst-2-smd]
  C1 = Ceramic Capacitor [capacitance=4.7µF voltage=16V package="100 mil [THT, multilayer]"]
  C2 = Ceramic Capacitor [capacitance=4.7µF voltage=16V package="100 mil [THT, multilayer]"]
  R1 = Resistor [tolerance=±5% resistance=2k package=THT]
  R2 = Resistor [tolerance=±5% resistance=220 package=THT]
  LED1 = LED - 5mm [color="Red (633nm)" package="5 mm [THT]"]
  C3 = Ceramic Capacitor [capacitance=10µF voltage=16V package="100 mil [THT, multilayer]"]
  R4 = Resistor [tolerance=±5% resistance=2M package=THT]
  R5 = Resistor [tolerance=±5% resistance=220 package=THT]
  C4 = Ceramic Capacitor [capacitance=10µF voltage=16V package="100 mil [THT, multilayer]"]
  L1 = Inductor [current=1.2 inductance=4.7µH package="400 mil [THT]"]
  C5 = Ceramic Capacitor [capacitance=22µF voltage=10V package="100 mil [THT, multilayer]"]
  R6 = Resistor [tolerance=±5% resistance=2M package=THT]
  R8 = Resistor [tolerance=±5% resistance=220 package=THT]
  C6 = Ceramic Capacitor [capacitance=100nF package="100 mil [THT, multilayer]"]
  J1 = female pin header, 3 pins [form="♀ (female)"]
  D1 = Diode [package=sma-diode_alt]
  R9 = Resistor [tolerance=±5% resistance=66.5 package=THT]
  R10 = Resistor [tolerance=±5% resistance=66.5 package=THT]
  D2 = Zener Diode [part_number=1N4732A breakdown_voltage=3.6V package="Melf DO-213 AB [SMD]"]
  D3 = Zener Diode [part_number=1N4732A breakdown_voltage=3.6V package="Melf DO-213 AB [SMD]"]
  R11 = Resistor [tolerance=±5% resistance=1.5k package=THT]
  C7 = Ceramic Capacitor [capacitance=4.7µF voltage=10V package="100 mil [THT, multilayer]"]
  C8 = Ceramic Capacitor [capacitance=0.1µF voltage=10V package="100 mil [THT, multilayer]"]
  J3 = female pin header, 1 pin [form="♀ (female)"]
  R12 = Resistor [tolerance=±5% resistance=330 package=THT]
  LED2 = LED - 5mm [color="Red (633nm)" package="5 mm [THT]"]
  R13 = Resistor [tolerance=±5% resistance=330 package=THT]
  LED3 = LED - 5mm [color="Red (633nm)" package="5 mm [THT]"]
  J2 = female pin header, 6 pins [form="♀ (female)"]

nets:
  N1: U1.Pin_1, J2.pin6
  N2: U1.Pin_2, R9.Pin_0, J2.pin4
  N3: U1.Pin_3, R10.Pin_0, J2.pin5
  GND: U1.Pin_4, X1.D+, U2.PGND, U2.GND, U2.PAD, U3.VSS, JP1.2, C1.0, R1.Pin_1, C3.0, R5.Pin_1, C5.0, R8.Pin_1, C6.0, J1.pin2, D2.anode, D3.anode, C7.0, C8.0, LED2.cathode, LED3.cathode
  N4: U1.Pin_5, J2.pin1
  N5: U1.Pin_6, R13.Pin_1, J2.pin2
  N6: U1.Pin_7, J2.pin3
  N7: U1.Pin_8, U2.VOUT, C5.1, R6.Pin_0, J1.pin3, R11.Pin_1, C7.1, C8.1, R12.Pin_1
  N8: X1.D-, D1.A
  N9: X1.GND, R10.Pin_1, D2.cathode
  N10: X1.VBUS, R9.Pin_1, D3.cathode, R11.Pin_0
  N11: U2.VAUX, C6.1
  N12: U2.L, L1.pin_0
  N13: U2.VIN, U3.VBAT, JP1.1, C2.1, C3.1, R4.Pin_0, C4.1, L1.pin_1
  N14: U2.EN, J3.pin1
  N15: U2.UVLO, R4.Pin_1, R5.Pin_0, C4.0
  N16: U2.FB, R6.Pin_1, R8.Pin_0
  N17: U3.STAT, R2.Pin_0
  N18: U3.VIN, C1.1, LED1.anode
  N19: U3.PROG, R1.Pin_0
  N20: R2.Pin_1, LED1.cathode
  N21: J1.pin1, D1.C
  N22: R12.Pin_0, LED2.anode
  N23: R13.Pin_0, LED3.anode

notes:
  Pin 0
  Pin 5
  Vin
  VCC 5v
  Micro USB jack
  PS Enable (pull low to turn off)
  JST jack for LiPo battery
  ATtiny85 power LED
  Charge power LED
  Pin 1 LED
